# Fritzing sketch fritz (saved by Fritzing 0.8.3b)
stripboards: 3

parts:
  SPKR1 = Loudspeaker  # not connected
  C1 = Electrolytic Capacitor [capacitance=10µF package="100 mil [THT, electrolytic]"]
  R1 = Resistor [tolerance=±5% resistance=10k package=THT]
  R2 = Resistor [tolerance=±5% resistance=10k package=THT]
  R3 = Resistor [tolerance=±5% resistance=10k package=THT]
  R4 = Resistor [tolerance=±5% resistance=10k package=THT]
  R5 = Resistor [tolerance=±5% resistance=10k package=THT]
  R6 = Resistor [tolerance=±5% resistance=10k package=THT]
  R7 = Resistor [tolerance=±5% resistance=10k package=THT]
  R8 = Resistor [tolerance=±5% resistance=10k package=THT]
  J1 = double row rounded female pin header, 14 pins [form="♀ (female rounded)"]
  R9 = Rotary Potentiometer (Large) [package=THT]
  Arduino_Due1 = Arduino DUE
  RGB_SMD_LED1 = SMD RGB LED (WS2812) [package=5050]
  Power_plug1 = Power plug  # not connected
  J2 = female pin header, 2 pins [form="♀ (female)"]
  J3 = female pin header, 2 pins [form="♀ (female)"]
  J4 = female pin header, 2 pins [form="♀ (female)"]
  J5 = female pin header, 8 pins [form="♀ (female)"]
  Arduino_Due2 = Arduino DUE
  RGB_SMD_LED2 = SMD RGB LED (WS2812) [package=5050]
  RGB_SMD_LED3 = SMD RGB LED (WS2812) [package=5050]
  RGB_SMD_LED4 = SMD RGB LED (WS2812) [package=5050]
  RGB_SMD_LED5 = SMD RGB LED (WS2812) [package=5050]
  RGB_SMD_LED6 = SMD RGB LED (WS2812) [package=5050]
  R10 = Resistor [tolerance=±5% resistance=10k package=THT]
  R11 = Resistor [tolerance=±5% resistance=10k package=THT]
  R12 = Resistor [tolerance=±5% resistance=10k package=THT]
  R13 = Resistor [tolerance=±5% resistance=10k package=THT]
  R14 = Resistor [tolerance=±5% resistance=10k package=THT]
  R15 = Resistor [tolerance=±5% resistance=10k package=THT]

nets:
  N1: C1.+, Arduino_Due1.DAC1
  N2: R1.Pin_0, R2.Pin_0, R3.Pin_0, R4.Pin_0, R5.Pin_0, R6.Pin_0, R7.Pin_0, R8.Pin_0, R10.Pin_0, R11.Pin_0, R12.Pin_0, R13.Pin_0, R14.Pin_0, R15.Pin_0
  N3: R1.Pin_1, Arduino_Due1.D36
  N4: R2.Pin_1, J1.pin2, Arduino_Due1.D34, J2.pin2
  N5: R3.Pin_1, J1.pin4, Arduino_Due1.D32, J3.pin2
  N6: R4.Pin_1, J1.pin6, Arduino_Due1.D30, J4.pin2
  N7: R5.Pin_1, J1.pin1, J1.pin3, J1.pin5, J1.pin7, J1.pin8, J1.pin9, J1.pin11, J1.pin13, Arduino_Due1.D28, J2.pin1, J3.pin1, J4.pin1, J5.pin1, J5.pin2, J5.pin3, J5.pin5, J5.pin7
  N8: R6.Pin_1, J1.pin10, Arduino_Due1.D26, J5.pin4
  N9: R7.Pin_1, J1.pin12, Arduino_Due1.D24, J5.pin6
  N10: R8.Pin_1, J1.pin14, Arduino_Due1.D22, J5.pin8
  N11: R9.leg1, Arduino_Due2.3.3V
  N12: R9.wiper, Arduino_Due2.A0
  N13: R9.leg2, Arduino_Due2.GROUND
  N14: Arduino_Due1.D1, Arduino_Due2.D0
  N15: Arduino_Due1.D0, Arduino_Due2.D1
  N16: Arduino_Due1.D38, Arduino_Due1.D40, Arduino_Due1.D42, Arduino_Due1.D44, Arduino_Due1.D46, Arduino_Due1.D48, R10.Pin_1, R11.Pin_1, R12.Pin_1, R13.Pin_1, R14.Pin_1, R15.Pin_1
  N17: RGB_SMD_LED1.VDD, Arduino_Due2.D24
  N18: Arduino_Due2.D26, RGB_SMD_LED2.VDD
  N19: Arduino_Due2.D28, RGB_SMD_LED3.VDD
  N20: Arduino_Due2.D30, RGB_SMD_LED6.VDD
  N21: Arduino_Due2.D32, RGB_SMD_LED4.VDD
  N22: Arduino_Due2.D34, RGB_SMD_LED5.VDD

custom parts:
  Arduino DUE: Arduino Due microcontroller. Breadboard based on photo taken from arduino.cc v1.1
  SMD RGB LED (WS2812): The WS2812 is an RGB LED with a WS2811 control IC built right into the LED. This really blew our minds to see the control IC of an individually addressable RGB LED was moved into the actual LED, so we wanted to offer this amazing product to you! They're great when you need a lot of color from not a lot of board space, now more so than ever.
